# Fritzing sketch Blynk (saved by Fritzing 0.9.3b)
breadboards: 1

parts:
  R1 = Resistor [tolerance=±5% resistance=220 package=THT]
  R2 = Resistor [tolerance=±5% resistance=220 package=THT]
  LED1 = LED - 5mm [color="Red (633nm)" package="5 mm [THT]"]
  LED2 = LED - 5mm [color="Green (560nm)" package="5 mm [THT]"]
  esp1 = ESP32 DevKitc V4
  DHT1 = Humidity and Temperature Sensor DHT11

nets:
  N1: R1.Pin_0, LED2.anode
  N2: R1.Pin_1, esp1.IO26
  N3: R2.Pin_0, LED1.anode
  N4: R2.Pin_1, esp1.IO27
  N5: LED1.cathode, LED2.cathode, esp1.GND, DHT1.GND_2
  N6: esp1.IO4, DHT1.Data-signal
  3V3: esp1.3V3, DHT1.Vcc

custom parts:
  ESP32 DevKitc V4: ESP32-DevKitC board with ESP32-WROOM-32 module. ESP32-DevKitC V4 is a small-sized ESP32-based development board produced by Espressif. Most of the pins on the ESP module are broken out to the pin headers on the board. The pins D0, D1, D2, D3, CMD and CLK are used internally for communication between ESP32 and SPI flash memory. They are grouped on both sides near the USB connector. Avoid using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
  Humidity and Temperature Sensor DHT11: Digital relative humidity & temperature sensor DHT11
