# Fritzing sketch Untitled Sketch (saved by Fritzing 0.9.3b)

parts:
  WeMos_D1_Mini1 = WeMos D1 Mini
  LED1 = LEDs [package=led10mm]
  AC_Source = Lilypad Battery Connect
  KY-1 = Keyes Relay [package=THT]

nets:
  N1: WeMos_D1_Mini1.5V, KY-1.power
  N2: WeMos_D1_Mini1.D2, KY-1.signal
  N3: WeMos_D1_Mini1.G, KY-1.ground
  N4: LED1.A, KY-1.NO
  N5: LED1.C, AC_Source.-
  N6: AC_Source.+, KY-1.C

custom parts:
  WeMos D1 Mini: The D1 mini is a mini wifi board based on ESP-8266EX.
  LEDs: LEDs Standard schematic elements and footprints for 5mm, 3mm, 1206, and 0603 sized LEDs. 5mm - Spark Fun Electronics SKU : COM-00529 (and others)
  Keyes Relay: The Keyes 5V relay module is suitable for SCM development, home appliance control. It uses a 5V~12V TIL control signal which can control DC / AC signal.
