# Fritzing sketch smart parking (saved by Fritzing 0.9.3b)
breadboards: 4

parts:
  esp1 = ESP32 DevKitc V4
  M1 = fc-51 [package=THT]
  M2 = fc-51 [package=THT]
  M3 = fc-51 [package=THT]
  M4 = fc-51 [package=THT]
  M5 = fc-51 [package=THT]
  M6 = fc-51 [package=THT]
  Part1 = RFID USB Reader
  LED1 = RGB LED - (4 legs) [package="5 mm [THT]"]
  LED2 = RGB LED - (4 legs) [package="5 mm [THT]"]
  LED3 = RGB LED - (4 legs) [package="5 mm [THT]"]
  LED4 = RGB LED - (4 legs) [package="5 mm [THT]"]
  LED5 = RGB LED - (4 legs) [package="5 mm [THT]"]
  LED6 = RGB LED - (4 legs) [package="5 mm [THT]"]
  M7 = Dagu DGServo 9g (Pan and tilt) [part_number=RS001B]
  Grove1 = Grove OLED 128x96

nets:
  N1: esp1.IO15, LED5.green_cathode
  N2: esp1.IO2, LED5.red_cathode
  N3: esp1.IO4, LED4.green_cathode
  N4: esp1.IO16, LED4.red_cathode
  N5: esp1.IO17, LED6.green_cathode
  N6: esp1.IO5, LED6.red_cathode
  N7: esp1.IO18, M7.pulse
  N8: esp1.IO21, Part1.TX-O, Grove1.SDA
  N9: esp1.IO22, Part1.TX-O-RS232, Grove1.SCL
  VCC: esp1.3V3, M1.pin3, M2.pin3, M3.pin3, M5.pin3, M6.pin3, Part1.VCC, M7.vcc, Grove1.VCC
  GND: esp1.EN, M1.pin2, M2.pin2, M3.pin2, M4.pin2, M5.pin2, M6.pin2, Part1.GND, LED1.common_anode, LED2.common_anode, LED3.common_anode, LED4.common_anode, LED5.common_anode, LED6.common_anode, M7.gnd, Grove1.GND
  N10: esp1.IO34, M2.pin1
  N11: esp1.IO35, M1.pin1
  N12: esp1.IO32, M3.pin1
  N13: esp1.IO33, M5.pin1
  N14: esp1.IO25, M6.pin1
  N15: esp1.IO26, M4.pin1
  N16: esp1.IO27, LED2.red_cathode
  N17: esp1.IO14, LED2.green_cathode
  N18: esp1.IO12, LED1.red_cathode
  N19: esp1.IO13, LED1.green_cathode
  N20: esp1.D1, LED3.red_cathode

custom parts:
  ESP32 DevKitc V4: ESP32-DevKitC board with ESP32-WROOM-32 module. ESP32-DevKitC V4 is a small-sized ESP32-based development board produced by Espressif. Most of the pins on the ESP module are broken out to the pin headers on the board. The pins D0, D1, D2, D3, CMD and CLK are used internally for communication between ESP32 and SPI flash memory. They are grouped on both sides near the USB connector. Avoid using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
